# Fritzing sketch AutoWaterDiagram (saved by Fritzing 0.9.3b)
breadboards: 1

parts:
  Part1 = Arduino Uno (Rev3)
  D1 = Diode [package=diode-hv]
  Q1 = NPN-Transistor [package="TO92 [THT]"]
  R1 = Resistor [tolerance=±5% resistance=220 package=THT]
  L1 = Solenoid
  Chirp!_Soil_Moisture_Sensor1 = Chirp! Soil Moisture Sensor v2.7.3

nets:
  N1: Part1.A0, Chirp!_Soil_Moisture_Sensor1.Pin_1
  N2: Part1.D7, R1.Pin_0
  N3: Part1.5V, Chirp!_Soil_Moisture_Sensor1.pin_3
  N4: Part1.GND, Q1.C, Chirp!_Soil_Moisture_Sensor1.pin_5
  N5: Part1.VIN, L1.pin2
  N6: D1.A, Q1.B, L1.pin1
  N7: Q1.E, R1.Pin_1
