# Fritzing sketch MoistureSensorDiagram (saved by Fritzing 0.9.3b)

parts:
  Arduino_Uno = Arduino Uno (Rev3)
  Moisture_Sensor = Chirp! Soil Moisture Sensor v2.7.3
  J1 = Dagu DGServo 9g header (male) [package=THT]  # not connected

nets:
  N1: Arduino_Uno.A0, Moisture_Sensor.Pin_0
  N2: Arduino_Uno.5V, Moisture_Sensor.pin_4
  N3: Arduino_Uno.GND, Moisture_Sensor.pin_2
