# Fritzing sketch SolenoidValveDiagram (saved by Fritzing 0.9.3b)
breadboards: 1

parts:
  Part1 = Arduino Uno (Rev3)
  D1 = Diode [package=diode-hv]
  Q1 = NPN-Transistor [package="TO92 [THT]"]
  R1 = Resistor [tolerance=±5% resistance=220 package=THT]
  L1 = Solenoid

nets:
  N1: Part1.D7, R1.Pin_0
  N2: Part1.GND, Q1.C
  N3: Part1.VIN, L1.pin2
  N4: D1.A, Q1.B, L1.pin1
  N5: Q1.E, R1.Pin_1
